# Fritzing sketch poulailler (saved by Fritzing 0.9.3b)
breadboards: 1

parts:
  MCU1 = Raspberry Pi Zero
  MOTOR1 = 28BYJ-48 Stepper Motor  # not connected
  X1 = X113647 Stepper Driver Board [package=board]
  DS1 = DS18B20 1-Wire Temperature Sensor [part_number=DS18B20]
  DS2 = DS18B20 1-Wire Temperature Sensor [part_number=DS18B20]
  S1 = Reed switch [package=THT]
  S2 = Reed switch [package=THT]
  S3 = Reed switch [package=THT]
  S4 = Reed switch [package=THT]
  S5 = Reed switch [package=THT]
  J1 = Power Jack [package=power_jack_smd]
  R1 = Resistor [tolerance=±5% resistance=4.7k package=THT]

nets:
  VDD: MCU1.pin_1, DS1.VDD, DS2.VDD
  GND: MCU1.pin_6, MCU1.pin_9, MCU1.pin_25, MCU1.pin_34, X1.GND, DS1.GND, DS2.GND, S1.pin_1, S2.pin_1, S3.pin_1, S4.pin_1, S5.pin_1, J1.GND
  N1: MCU1.pin_7, R1.Pin_1
  N2: MCU1.pin_11, S1.pin_2
  N3: MCU1.pin_13, S2.pin_2
  N4: MCU1.pin_15, S3.pin_2
  N5: MCU1.pin_16, S4.pin_2
  N6: MCU1.pin_18, S5.pin_2
  N7: MCU1.pin_29, X1.IN1
  N8: MCU1.pin_31, X1.IN2
  N9: MCU1.pin_33, X1.IN3
  N10: MCU1.pin_35, X1.IN4
  N11: X1.+V, J1.GNDBREAK
  N12: DS1.DQ, DS2.DQ, R1.Pin_0

custom parts:
  28BYJ-48 Stepper Motor: 28BYJ-48 gear-reduction stepper motor (small)
  X113647 Stepper Driver Board: A common stepper motor driver board based on ULN2003APG darlington array
